# Fritzing sketch talk_a_lot_fritz (saved by Fritzing 0.8.3b)
stripboards: 1
breadboards: 1

parts:
  S1 = Pushbutton [package="[THT]"]
  Dot_Matrix1 = LED Dot Matrix 18mm (0.7 INCH)  # not connected
  Dot_Matrix2 = LED Dot Matrix 18mm (0.7 INCH)  # not connected
  TRS1 = Audio Jack (TRS) 3.5mm [package="4Ucon 08780 [THT]"]
  SPKR1 = Loudspeaker
  S2 = Pushbutton [package="[THT]"]
  LED1 = LED - 5mm [color="Red (633nm)" package="5 mm [THT]"]
  LED2 = LED - 5mm [color="Red (633nm)" package="5 mm [THT]"]
  S3 = Pushbutton [package="[THT]"]
  LED3 = LED - 5mm [color="Red (633nm)" package="5 mm [THT]"]
  Part1 = Arduino Uno (Rev3)

nets (from the schematic view):
  N1: S1.Pin_1, S1.Pin_2, S2.Pin_1, S2.Pin_2, S3.Pin_1, S3.Pin_2, Part1.GND
  N2: S1.Pin_3, S1.Pin_4, LED1.cathode
  N3: TRS1.Sleeve, SPKR1.pin1
  N4: TRS1.Ring, TRS1.Tip, SPKR1.pin2
  N5: S2.Pin_3, S2.Pin_4, LED2.anode, Part1.D1/TX
  N6: LED1.anode, Part1.ICSP_MOSI, Part1.D11_PWM/MOSI
  N7: S3.Pin_3, S3.Pin_4, LED3.cathode
  N8: LED3.anode, Part1.D0/RX
  N9: Part1.ioref, Part1.5V

notes:
  The blank board represents the Ada-fruit wave-shield. For simplicity I will represent it as simply the connector for a speaker. In reality it is the main audio component of this project, housing the SDCard and all audio processing components.
  Ada-fruit I2C matrix blocks. Are used to simulate eye movement.
  User input comes in the form of buttons. As the user interacts witht the bot, its voice reacts. Irrationally!
